// Logisim project microOrgaSmallI.circ as structural Verilog: 10 circuits, main circuit microOrgaSmallI
module microOrgaSmallI (
  input  reset,
  input  mem_clear
);

  wire ALU_enA, ALU_enB, ALU_enOut, ALU_opW, button_1_out, button_2_out, button_3_out, clk, clock_1_out, clr,
       DE_enOutImm, DE_load_7_0, DE_load_15_8, i, IC_cli, IC_inta, IC_sti, \int , intr, MM_enAddr, MM_enOut,
       MM_load, MP_enOut, PC_enOut, PC_inc, PC_load, RB_enIn, RB_enOut, RB_selectIndexIn, RB_selectIndexOut,
       rst;
  wire [2:0] flags, MP_op, multiplexer_1_out, multiplexer_2_out, X, Y;
  wire [3:0] ALU_OP;
  wire [4:0] OP;
  wire [7:0] A, B, M, O, PC, PC_outvalue;
  wire [8:0] M_PC;
  wire [15:0] INST;
  wire [31:0] R0_3, R4_7;

  PC u_PC (
    .load(PC_load), .inc(PC_inc), .outValue(PC_outvalue), .enOut(PC_enOut), .VIEW_value(PC), .clk(clk),
    .rst(rst), .inValue(PC_outvalue));
  Registers Registers (
    .clk(clk), .rst(rst), .inData(PC_outvalue), .outData(PC_outvalue), .enIn(RB_enIn), .enOut(RB_enOut),
    .inSelect(multiplexer_1_out), .outSelect(multiplexer_2_out), .VIEW_R4_R7(R4_7), .VIEW_R0_R3(R0_3));
  Memory Memory (
    .addr(PC_outvalue), .load(MM_load), .outData(PC_outvalue), .enOut(MM_enOut), .clk(clk), .rst(rst),
    .inData(PC_outvalue), .enAddr(MM_enAddr), .clr(clr));
  assign PC_outvalue = DE_enOutImm ? M : 8'bz;  // Controlled_Buffer controlled_buffer_1
  Decode Decode (
    .indexX(X), .indexY(Y), .valueM(M), .opcode(OP), .clk(clk), .rst(rst), .halfInst(PC_outvalue),
    .loadH(DE_load_15_8), .loadL(DE_load_7_0), .VIEW_Inst(INST));
  MemoryPlus MemoryPlus (
    .mem_op(MP_op), .inData(PC_outvalue), .wrAddr(PC_outvalue), .rdAddr(PC_outvalue), .clk(clk), .rst(rst),
    .clr(clr), .outData(PC_outvalue), .enOut(MP_enOut));
  Hex_Digit_Display hex_digit_display_1 (.value(PC_outvalue[7:4]));  // open: dp
  Multiplexer #(.width(3), .enable("false")) multiplexer_1 (
    .in0(X), .in1(Y), .out(multiplexer_1_out), .sel(RB_selectIndexIn));
  Multiplexer #(.width(3), .enable("false")) multiplexer_2 (
    .in0(X), .in1(Y), .out(multiplexer_2_out), .sel(RB_selectIndexOut));
  Hex_Digit_Display hex_digit_display_2 (.value(PC_outvalue[3:0]));  // open: dp
  InterruptController interruptcontroller_1 (
    .STI(IC_sti), .CLI(IC_cli), .INTA(IC_inta), .INTR(intr), .I(i), .clk(clk), .rst(rst), .INT(\int ));
  ControlUnit controlunit_1 (
    .RB_enIn(RB_enIn), .RB_enOut(RB_enOut), .RB_selectIndexIn(RB_selectIndexIn),
    .RB_selectIndexOut(RB_selectIndexOut), .MM_enOut(MM_enOut), .MM_load(MM_load), .MM_enAddr(MM_enAddr),
    .ALU_enA(ALU_enA), .ALU_enB(ALU_enB), .ALU_enOut(ALU_enOut), .ALU_opW(ALU_opW), .PC_load(PC_load),
    .PC_inc(PC_inc), .PC_enOut(PC_enOut), .DE_loadH(DE_load_15_8), .inOpcode(OP), .DE_enOutImm(DE_enOutImm),
    .VIEW_microOpAddr(M_PC), .clk(clk), .rst(rst), .flags(flags), .DE_loadL(DE_load_7_0), .IC_sti(IC_sti),
    .IC_cli(IC_cli), .IC_inta(IC_inta), .INTR(intr), .MP_op(MP_op), .ALU_OP(ALU_OP), .MP_enOut(MP_enOut));
  ALU alu_1 (
    .A(PC_outvalue), .enA(ALU_enA), .B(PC_outvalue), .enB(ALU_enB), .OP(ALU_OP), .out(PC_outvalue),
    .opW(ALU_opW), .enOut(ALU_enOut), .VIEW_out(O), .VIEW_A(A), .VIEW_B(B), .flags(flags), .clk(clk),
    .rst(rst), .shift(Y));
  LED Z (.in(flags[1]));
  LED N (.in(flags[2]));
  Hex_Digit_Display hex_digit_display_3 (.value(INST[15:12]));  // open: dp
  Hex_Digit_Display hex_digit_display_4 (.value(M[7:4]));  // open: dp
  LED u_I (.in(i));
  LED C (.in(flags[0]));
  Hex_Digit_Display hex_digit_display_5 (.value(R0_3[7:4]));  // open: dp
  Hex_Digit_Display hex_digit_display_6 (.value(R0_3[3:0]));  // open: dp
  Hex_Digit_Display hex_digit_display_7 (.value(R0_3[11:8]));  // open: dp
  Hex_Digit_Display hex_digit_display_8 (.value(R0_3[15:12]));  // open: dp
  Hex_Digit_Display hex_digit_display_9 (.value(R0_3[19:16]));  // open: dp
  Hex_Digit_Display hex_digit_display_10 (.value(R0_3[23:20]));  // open: dp
  Hex_Digit_Display hex_digit_display_11 (.value(R0_3[27:24]));  // open: dp
  Hex_Digit_Display hex_digit_display_12 (.value(R0_3[31:28]));  // open: dp
  Hex_Digit_Display hex_digit_display_13 (.value(INST[11:8]));  // open: dp
  Hex_Digit_Display hex_digit_display_14 (.value(M[3:0]));  // open: dp
  Button button_1 (.out(button_1_out));
  Clock clock_1 (.out(clock_1_out));
  Hex_Digit_Display hex_digit_display_15 (.value(INST[7:4]));  // open: dp
  Hex_Digit_Display hex_digit_display_16 (.value(INST[3:0]));  // open: dp
  Hex_Digit_Display hex_digit_display_17 (.value({1'b0, X}));  // open: dp
  or or_1 (clk, button_1_out, clock_1_out);
  Hex_Digit_Display hex_digit_display_18 (.value(R4_7[7:4]));  // open: dp
  Hex_Digit_Display hex_digit_display_19 (.value(R4_7[3:0]));  // open: dp
  Hex_Digit_Display hex_digit_display_20 (.value(R4_7[15:12]));  // open: dp
  Hex_Digit_Display hex_digit_display_21 (.value(R4_7[11:8]));  // open: dp
  Hex_Digit_Display hex_digit_display_22 (.value(R4_7[19:16]));  // open: dp
  Hex_Digit_Display hex_digit_display_23 (.value(R4_7[23:20]));  // open: dp
  Hex_Digit_Display hex_digit_display_24 (.value(R4_7[27:24]));  // open: dp
  Hex_Digit_Display hex_digit_display_25 (.value(R4_7[31:28]));  // open: dp
  Hex_Digit_Display hex_digit_display_26 (.value({3'b000, M_PC[8]}));  // open: dp
  Hex_Digit_Display hex_digit_display_27 (.value({1'b0, Y}));  // open: dp
  Button button_2 (.out(button_2_out));
  or or_2 (rst, button_2_out, reset);
  Hex_Digit_Display hex_digit_display_28 (.value(M_PC[7:4]));  // open: dp
  Hex_Digit_Display hex_digit_display_29 (.value({3'b000, OP[4]}));  // open: dp
  Button button_3 (.out(button_3_out));
  or or_3 (clr, button_3_out, mem_clear);
  Hex_Digit_Display hex_digit_display_30 (.value(PC[7:4]));  // open: dp
  Hex_Digit_Display hex_digit_display_31 (.value(PC[3:0]));  // open: dp
  Hex_Digit_Display hex_digit_display_32 (.value(A[3:0]));  // open: dp
  Hex_Digit_Display hex_digit_display_33 (.value(A[7:4]));  // open: dp
  Hex_Digit_Display hex_digit_display_34 (.value(B[3:0]));  // open: dp
  Hex_Digit_Display hex_digit_display_35 (.value(B[7:4]));  // open: dp
  Hex_Digit_Display hex_digit_display_36 (.value(O[3:0]));  // open: dp
  Hex_Digit_Display hex_digit_display_37 (.value(O[7:4]));  // open: dp
  Hex_Digit_Display hex_digit_display_38 (.value(M_PC[3:0]));  // open: dp
  Hex_Digit_Display hex_digit_display_39 (.value(OP[3:0]));  // open: dp
  Button button_4 (.out(\int ));

  // Notes on the sheet:
  //   BUS
  //   Instrucción
  //   value M
  //   R0
  //   R1
  //   R2
  //   R3
  //   index X
  //   R4
  //   R5
  //   R6
  //   R7
  //   microPC
  //   index Y
  //   Opcode
  //   PC
  //   A
  //   B
  //   OUT
endmodule

module Registers (
  input  clk,
  input  rst,
  input  [7:0] inData,
  input  enOut,
  input  enIn,
  input  [2:0] outSelect,
  input  [2:0] inSelect,
  output [31:0] VIEW_R0_R3,
  output [31:0] VIEW_R4_R7,
  output [7:0] outData
);

  wire decoder_1_out0, decoder_1_out1, decoder_1_out2, decoder_1_out3, decoder_1_out4, decoder_1_out5,
       decoder_1_out6, decoder_1_out7;
  wire [7:0] multiplexer_1_out;

  Decoder #(.select(3), .disabled(0)) decoder_1 (
    .out0(decoder_1_out0), .out1(decoder_1_out1), .out2(decoder_1_out2), .out3(decoder_1_out3),
    .out4(decoder_1_out4), .out5(decoder_1_out5), .out6(decoder_1_out6), .out7(decoder_1_out7),
    .sel(inSelect), .en(enIn));
  Register R0 (.D(inData), .en(decoder_1_out0), .Q(VIEW_R0_R3[7:0]), .clk(clk), .clr(rst));
  Register R1 (.D(inData), .en(decoder_1_out1), .Q(VIEW_R0_R3[15:8]), .clk(clk), .clr(rst));
  Register R2 (.D(inData), .en(decoder_1_out2), .Q(VIEW_R0_R3[23:16]), .clk(clk), .clr(rst));
  Register R3 (.D(inData), .en(decoder_1_out3), .Q(VIEW_R0_R3[31:24]), .clk(clk), .clr(rst));
  Register R4 (.D(inData), .en(decoder_1_out4), .Q(VIEW_R4_R7[7:0]), .clk(clk), .clr(rst));
  Register R5 (.D(inData), .en(decoder_1_out5), .Q(VIEW_R4_R7[15:8]), .clk(clk), .clr(rst));
  Register R6 (.D(inData), .en(decoder_1_out6), .Q(VIEW_R4_R7[23:16]), .clk(clk), .clr(rst));
  Register R7 (.D(inData), .en(decoder_1_out7), .Q(VIEW_R4_R7[31:24]), .clk(clk), .clr(rst));
  assign outData = enOut ? multiplexer_1_out : 8'bz;  // Controlled_Buffer controlled_buffer_1
  Multiplexer #(.select(3), .width(8), .enable("false")) multiplexer_1 (
    .in0(VIEW_R0_R3[7:0]), .in1(VIEW_R0_R3[15:8]), .in2(VIEW_R0_R3[23:16]), .in3(VIEW_R0_R3[31:24]),
    .in4(VIEW_R4_R7[7:0]), .in5(VIEW_R4_R7[15:8]), .in6(VIEW_R4_R7[23:16]), .in7(VIEW_R4_R7[31:24]),
    .out(multiplexer_1_out), .sel(outSelect));
endmodule

module PC (
  input  clk,
  input  rst,
  input  load,
  input  [7:0] inValue,
  input  inc,
  input  enOut,
  output [7:0] VIEW_value,
  output [7:0] outValue
);

  assign outValue = enOut ? VIEW_value : 8'bz;  // Controlled_Buffer controlled_buffer_1
  Counter counter_1 (.load(load), .D(inValue), .count(inc), .Q(VIEW_value), .clk(clk), .clr(rst));  // open: carry
endmodule

module ALU (
  input  clk,
  input  rst,
  input  [7:0] A,
  input  enA,
  input  [7:0] B,
  input  enB,
  input  opW,
  input  enOut,
  input  [2:0] shift,
  input  [3:0] OP,
  output [2:0] flags,
  output [7:0] out,
  output [7:0] VIEW_out,
  output [7:0] VIEW_A,
  output [7:0] VIEW_B
);

  wire adder_1_cout, adder_2_cout, nor_1_out, not_1_out, not_2_out, not_3_out, not_4_out, or_2_out, or_3_out,
       subtractor_2_bout;
  wire [7:0] adder_1_out, adder_2_out, and_1_out, mixer_1_out_3, multiplexer_1_out, or_1_out, shifter_1_out,
       shifter_2_out, subtractor_1_out, subtractor_2_out, xor_1_out;

  Register ALU_IN_A (.D(A), .en(enA), .Q(VIEW_A), .clk(clk), .clr(rst));
  Register ALU_IN_B (.D(B), .en(enB), .Q(VIEW_B), .clk(clk), .clr(rst));
  Adder adder_1 (.a(VIEW_A), .b(VIEW_B), .out(adder_1_out), .cin(1'b0), .cout(adder_1_cout));
  Adder adder_2 (.a(VIEW_A), .b(VIEW_B), .out(adder_2_out), .cin(flags[0]), .cout(adder_2_cout));
  Subtractor subtractor_1 (.a(VIEW_A), .b(VIEW_B), .out(subtractor_1_out), .bin(1'b0));  // open: bout
  assign and_1_out = VIEW_A & VIEW_B;  // AND_Gate and_1, 8 bits wide
  assign or_1_out = VIEW_A | VIEW_B;  // OR_Gate or_1, 8 bits wide
  assign xor_1_out = VIEW_A ^ VIEW_B;  // XOR_Gate xor_1, 8 bits wide
  Subtractor subtractor_2 (.a(VIEW_A), .b(VIEW_B), .out(subtractor_2_out), .bin(1'b0), .bout(subtractor_2_bout));
  Shifter #(.shift("lr")) shifter_1 (.in(VIEW_A), .\dist (shift), .out(shifter_1_out));
  Shifter shifter_2 (.in(VIEW_A), .\dist (shift), .out(shifter_2_out));
  Mixer mixer_1 (.A(VIEW_A), .B(VIEW_B), .out_3(mixer_1_out_3));
  or or_2 (or_2_out, adder_1_cout, adder_2_cout, subtractor_2_bout);
  Register #(.width(1)) C (.D(or_2_out), .en(opW), .Q(flags[0]), .clk(not_1_out), .clr(rst));
  not not_1 (not_1_out, clk);
  not not_2 (not_2_out, clk);
  nor nor_1 (nor_1_out, multiplexer_1_out[0], multiplexer_1_out[1], multiplexer_1_out[2], multiplexer_1_out[3], multiplexer_1_out[4], multiplexer_1_out[5], multiplexer_1_out[6], multiplexer_1_out[7]);
  Register #(.width(1)) Z (.D(nor_1_out), .en(opW), .Q(flags[1]), .clk(not_2_out), .clr(rst));
  Multiplexer #(.select(4), .width(8), .enable("false")) multiplexer_1 (
    .in0({8{1'b0}}), .in1(adder_1_out), .in2(adder_2_out), .in3(subtractor_1_out), .in4(and_1_out),
    .in5(or_1_out), .in6(xor_1_out), .in7(subtractor_2_out), .in8(shifter_1_out), .in9(shifter_2_out),
    .in10({8{1'b0}}), .in11(mixer_1_out_3), .in12({8{1'b0}}), .in13(8'h1), .in14(8'h2), .in15({8{1'b1}}),
    .out(multiplexer_1_out), .sel(OP));
  or or_3 (or_3_out, OP[3], OP[2], OP[1], OP[0]);
  not not_3 (not_3_out, clk);
  Register #(.width(1)) N (.D(multiplexer_1_out[7]), .en(opW), .Q(flags[2]), .clk(not_4_out), .clr(rst));
  not not_4 (not_4_out, clk);
  Register ALU_OUT (.D(multiplexer_1_out), .en(or_3_out), .Q(VIEW_out), .clk(not_3_out), .clr(rst));
  assign out = enOut ? VIEW_out : 8'bz;  // Controlled_Buffer controlled_buffer_1

  // Other names for the same wires on the sheet: write_op = opW

  // Notes on the sheet:
  //   FLAGS
  //   cte 0x00 = 1100
  //   cte 0x01 = 1101
  //   cte 0x02 = 1110
  //   cte 0xFF = 1111
  //   ADD = 0001
  //   ADC = 0010
  //   SUB = 0011
  //   AND = 0100
  //   OR = 0101
  //   XOR =0110
  //   CMP = 0111
  //   SHR = 1000
  //   SHL = 1001
  //   CONSTANTES
endmodule

module Memory (
  input  clk,
  input  rst,
  input  clr,
  input  [7:0] addr,
  input  enAddr,
  input  enOut,
  input  [7:0] inData,
  input  load,
  output [7:0] outData
);

  wire [7:0] addr_q, ram_1_data;

  Register u_addr (.D(addr), .en(enAddr), .Q(addr_q), .clk(clk), .clr(rst));
  RAM #(.bus("separate")) ram_1 (
    .addr(addr_q), .din(inData), .data(ram_1_data), .str(load), .clk(clk), .clr(clr));  // open: sel, ld
  assign outData = enOut ? ram_1_data : 8'bz;  // Controlled_Buffer controlled_buffer_1
endmodule

module MemoryPlus (
  input  [2:0] mem_op,
  input  clk,
  input  rst,
  input  clr,
  input  [7:0] inData,
  input  enOut,
  input  [7:0] wrAddr,
  input  [7:0] rdAddr,
  output [7:0] outData
);

  wire add, clr_t, en_rdAddr, en_wrAddr, en_wrValue, load, mem_str, mov, nclk, prd;
  wire [7:0] adder_1_out, mem_in, mem_out, multiplexer_2_out, multiplier_1_out, rdAddr_out, rdValue_out,
       wrAddr_out, wrValue_in, wrValue_out;

  Decoder #(.select(3), .enable("false")) decoder_1 (
    .out1(en_wrAddr), .out2(en_rdAddr), .out3(load), .out4(add), .out5(prd), .out6(clr_t), .out7(mov),
    .sel(mem_op));  // open: out0
  not not_1 (nclk, clk);
  Adder adder_1 (.a(wrValue_out), .b(rdValue_out), .out(adder_1_out));  // open: cin, cout
  Multiplier multiplier_1 (.a(wrValue_out), .b(rdValue_out), .out(multiplier_1_out));  // open: cin, cout
  Register u_wrAddr (.D(wrAddr), .en(en_wrAddr), .Q(wrAddr_out), .clk(clk), .clr(rst));
  Register u_rdAddr (.D(rdAddr), .en(en_rdAddr), .Q(rdAddr_out), .clk(clk), .clr(rst));
  Multiplexer #(.select(3), .width(8), .enable("false")) multiplexer_1 (
    .in3(inData), .in4(adder_1_out), .in5(multiplier_1_out), .in6({8{1'b0}}), .in7(rdValue_out),
    .out(mem_in), .sel(mem_op));  // open: in0, in1, in2
  or or_1 (mem_str, load, add, prd, clr_t, mov);
  or or_2 (en_wrValue, en_wrAddr, mem_str);
  Multiplexer #(.width(8), .enable("false")) multiplexer_2 (
    .in0(wrAddr_out), .in1(rdAddr_out), .out(multiplexer_2_out), .sel(en_rdAddr));
  assign outData = enOut ? rdValue_out : 8'bz;  // Controlled_Buffer controlled_buffer_1
  Multiplexer #(.select(3), .width(8), .enable("false")) multiplexer_3 (
    .in1(mem_out), .in3(mem_in), .in4(mem_in), .in5(mem_in), .in6(mem_in), .in7(mem_in), .out(wrValue_in),
    .sel(mem_op));  // open: in0, in2
  RAM #(.bus("separate")) ram_1 (
    .addr(multiplexer_2_out), .din(mem_in), .data(mem_out), .str(mem_str), .clk(clk), .clr(clr));  // open: sel, ld
  Register wrValue (.D(wrValue_in), .en(en_wrValue), .Q(wrValue_out), .clk(nclk), .clr(rst));
  Register rdValue (.D(mem_out), .en(en_rdAddr), .Q(rdValue_out), .clk(nclk), .clr(rst));

  // Other names for the same wires on the sheet: clr_ext = clr
endmodule

module Decode (
  input  clk,
  input  rst,
  input  [7:0] halfInst,
  input  loadL,
  input  loadH,
  output [4:0] opcode,
  output [2:0] indexX,
  output [2:0] indexY,
  output [7:0] valueM,
  output [15:0] VIEW_Inst
);

  Register IR_7_0 (.D(halfInst), .en(loadL), .Q(VIEW_Inst[7:0]), .clk(clk), .clr(rst));
  Register IR_15_8 (.D(halfInst), .en(loadH), .Q(VIEW_Inst[15:8]), .clk(clk), .clr(rst));
  Register #(.width(5)) u_opcode (.D(VIEW_Inst[15:11]), .en(1'b1), .Q(opcode), .clk(clk), .clr(rst));
  Register #(.width(3)) index_X (.D(VIEW_Inst[10:8]), .en(1'b1), .Q(indexX), .clk(clk), .clr(rst));
  Register #(.width(3)) index_Y (.D(VIEW_Inst[7:5]), .en(1'b1), .Q(indexY), .clk(clk), .clr(rst));
  Register Mem_Or_Imm (.D(VIEW_Inst[7:0]), .en(1'b1), .Q(valueM), .clk(clk), .clr(rst));
endmodule

module ControlUnit (
  input  clk,
  input  rst,
  input  [2:0] flags,
  input  [4:0] inOpcode,
  input  INTR,
  output RB_enIn,
  output RB_enOut,
  output RB_selectIndexIn,
  output RB_selectIndexOut,
  output MM_enOut,
  output MM_load,
  output MM_enAddr,
  output ALU_enA,
  output ALU_enB,
  output ALU_enOut,
  output ALU_opW,
  output [3:0] ALU_OP,
  output [2:0] MP_op,
  output PC_load,
  output PC_inc,
  output PC_enOut,
  output MP_enOut,
  output DE_enOutImm,
  output DE_loadL,
  output DE_loadH,
  output IC_sti,
  output IC_cli,
  output IC_inta,
  output [8:0] VIEW_microOpAddr
);

  wire and_1_out, and_2_out, and_3_out, en_mem_op, I_microOp, jc_microOp, jn_microOp, jz_microOp,
       load_microOp, not_1_out, or_1_out, or_2_out, or_3_out, reset_microOp;
  wire [3:3] demultiplexer_1_out1;
  wire [8:0] adder_1_out, adder_2_out, adder_3_out, adder_4_out, multiplexer_1_out, multiplexer_2_out,
       multiplexer_3_out, multiplexer_4_out;
  wire [15:12] rom_1_data;

  Counter #(.width(9), .max('h1ff)) microPC (
    .load(load_microOp), .D(multiplexer_4_out), .count(not_1_out), .Q(VIEW_microOpAddr), .clk(clk),
    .clr(or_1_out));  // open: carry
  not not_1 (not_1_out, load_microOp);
  or or_1 (or_1_out, reset_microOp, rst);
  and and_1 (and_1_out, flags[1], jz_microOp);
  and and_2 (and_2_out, flags[2], jn_microOp);
  or or_2 (or_2_out, and_2_out, and_1_out, and_3_out);
  Adder #(.width(9)) adder_1 (.a(VIEW_microOpAddr), .b(9'h1), .out(adder_1_out), .cin(1'b0));  // open: cout
  Adder #(.width(9)) adder_2 (.a(VIEW_microOpAddr), .b(9'h2), .out(adder_2_out), .cin(1'b0));  // open: cout
  Adder #(.width(9)) adder_3 (.a(VIEW_microOpAddr), .b(9'h1), .out(adder_3_out), .cin(1'b0));  // open: cout
  Adder #(.width(9)) adder_4 (.a(VIEW_microOpAddr), .b(9'h7), .out(adder_4_out), .cin(1'b0));  // open: cout
  and and_3 (and_3_out, flags[0], jc_microOp);
  or or_3 (or_3_out, jn_microOp, jz_microOp, jc_microOp);
  Multiplexer #(.width(9), .enable("false")) multiplexer_1 (
    .in0(adder_1_out), .in1(adder_2_out), .out(multiplexer_1_out), .sel(or_2_out));
  Multiplexer #(.width(9), .enable("false")) multiplexer_2 (
    .in0(adder_3_out), .in1(adder_4_out), .out(multiplexer_2_out), .sel(INTR));
  Multiplexer #(.width(9), .enable("false")) multiplexer_3 (
    .in0({inOpcode, 4'b0000}), .in1(multiplexer_1_out), .out(multiplexer_3_out), .sel(or_3_out));
  Multiplexer #(.width(9), .enable("false")) multiplexer_4 (
    .in0(multiplexer_3_out), .in1(multiplexer_2_out), .out(multiplexer_4_out), .sel(I_microOp));
  ROM #(.addrWidth(9), .dataWidth(32)) rom_1 (
    .addr(VIEW_microOpAddr),
    .data({reset_microOp, load_microOp, IC_inta, IC_cli, IC_sti, DE_loadH, DE_loadL, DE_enOutImm, MP_enOut, PC_enOut, PC_inc, PC_load, I_microOp, jn_microOp, jz_microOp, jc_microOp, rom_1_data, ALU_opW, ALU_enOut, ALU_enB, ALU_enA, en_mem_op, MM_enAddr, MM_load, MM_enOut, RB_selectIndexOut, RB_selectIndexIn, RB_enOut, RB_enIn}));  // open: sel
  Demultiplexer #(.width(4), .disabled(0), .enable("false")) demultiplexer_1 (
    .out0(ALU_OP), .out1({demultiplexer_1_out1[3], MP_op}), .in(rom_1_data), .sel(en_mem_op));

  // Notes on the sheet:
  //   X
  //   contents of rom_1 (hex, n*v repeats v):
  //   40080000 400040 4200010 400040 2200010 40000000 80000000 f000 440 30400020 c000 440 100010 80000000
  //   0 0 102 20a 1800 401 80000000 11*0 102 20a 2800 401 80000000 11*0 102 20a 3800 401 80000000 11*0 102
  //   20a 4800 401 80000000 11*0 102 20a 5800 401 80000000 11*0 102 20a 6800 401 80000000 11*0 102 20a
  //   7800 80000000 12*0 b 80000000 14*0 102 d000 600 1800 401 80000000 10*0 102 f000 600 6000 500 d000
  //   600 1000 401 80000000 6*0 102 20a b800 401 80000000 11*0 80000000 15*0 80000000 15*0 80000000 15*0
  //   80000000 15*0 1000040 22 80000000 13*0 1000040 11 80000000 13*0 42 2a 80000000 13*0 4a 11 80000000
  //   13*0 1100000 80000000 14*0 40010000 80000000 1100000 80000000 12*0 40020000 80000000 1100000
  //   80000000 12*0 40040000 80000000 1100000 80000000 12*0 102 d800 600 1800 401 80000000 10*0 102 d800
  //   600 3800 401 80000000 10*0 102 8800 401 80000000 12*0 102 9800 401 80000000 12*0 8000000 80000000
  //   14*0 10000000 80000000 14*0 f000 440 8100010 80000000 12*0 1000001 80000000
endmodule

module Mixer (
  input  [7:0] A,
  input  [7:0] B,
  output [7:0] out_3
);


  assign out_3 = {B[1], A[6], B[3], A[4], B[5], A[2], B[7], A[0]};
endmodule

module InterruptController (
  input  clk,
  input  rst,
  input  STI,
  input  CLI,
  input  INT,
  input  INTA,
  output I,
  output INTR
);

  wire INT_q, or_1_out, or_2_out;

  Register #(.width(1)) u_I (.D(1'b1), .en(STI), .Q(I), .clk(clk), .clr(or_1_out));
  Register #(.width(1)) u_INT (.D(1'b1), .en(1'b1), .Q(INT_q), .clk(INT), .clr(or_2_out));
  or or_1 (or_1_out, CLI, rst);
  or or_2 (or_2_out, INTA, rst);
  and and_1 (INTR, I, INT_q);
endmodule
