// Logisim project Práctica2.circ as structural Verilog: 19 circuits, main circuit NAND_AND
module NAND_AND (
  input  p,
  input  q,
  output pANDq
);

  wire nand_1_out;

  nand nand_1 (nand_1_out, p, q);
  nand nand_2 (pANDq, nand_1_out, nand_1_out);
endmodule

module NAND_NOT (
  input  p,
  output NOTp
);

  nand nand_1 (NOTp, p, p);
endmodule

module NAND_OR (
  input  p,
  input  q,
  output pORq
);

  wire nand_1_out, nand_2_out;

  nand nand_1 (nand_1_out, p, p);
  nand nand_2 (nand_2_out, q, q);
  nand nand_3 (pORq, nand_1_out, nand_2_out);
endmodule

module NOR_NOT (
  input  p,
  output NOTp
);

  nor nor_1 (NOTp, p, p);
endmodule

module NOR_AND (
  input  p,
  input  q,
  output pANDq
);

  wire nor_1_out, nor_2_out;

  nor nor_1 (nor_1_out, p, p);
  nor nor_2 (nor_2_out, q, q);
  nor nor_3 (pANDq, nor_1_out, nor_2_out);
endmodule

module NOR_OR (
  input  p,
  input  q,
  output pORq
);

  wire nor_1_out;

  nor nor_1 (nor_1_out, p, q);
  nor nor_2 (pORq, nor_1_out, nor_1_out);
endmodule

module P2_EJ5 (
  input  p,
  input  q,
  input  r,
  output pANDqANDr
);

  wire nor_1_out, not_1_out, not_2_out, not_3_out, not_4_out;

  not not_1 (not_1_out, p);
  not not_2 (not_2_out, q);
  not not_3 (not_3_out, r);
  nor nor_1 (nor_1_out, not_1_out, not_2_out);
  not not_4 (not_4_out, nor_1_out);
  nor nor_2 (pANDqANDr, not_4_out, not_3_out);
endmodule

module P2_EJ6 (
  input  A,
  input  B,
  input  C,
  output RES
);

  wire and_1_out, and_2_out, not_1_out;

  not not_1 (not_1_out, B);
  and and_1 (and_1_out, A, not_1_out);
  and and_2 (and_2_out, B, C);
  or or_1 (RES, and_1_out, and_2_out);
endmodule

module DemultiplexorV1 (
  input  e0,
  input  c1,
  input  c0,
  output s3,
  output s2,
  output s1,
  output s0
);

  wire and_1_out, and_3_out, and_5_out, and_7_out, not_1_out, not_2_out;

  not not_1 (not_1_out, c1);
  not not_2 (not_2_out, c0);
  and and_1 (and_1_out, c1, c0);
  and and_2 (s3, and_1_out, e0);
  and and_3 (and_3_out, c1, not_2_out);
  and and_4 (s2, and_3_out, e0);
  and and_5 (and_5_out, not_1_out, c0);
  and and_6 (s1, and_5_out, e0);
  and and_7 (and_7_out, not_1_out, not_2_out);
  and and_8 (s0, and_7_out, e0);
endmodule

module DemultiplexorV2 (
  input  e0,
  input  c1,
  input  c0,
  output s3,
  output s2,
  output s1,
  output s0
);

  wire decodificador_1_s0, decodificador_1_s1, decodificador_1_s2, decodificador_1_s3;

  Decodificador decodificador_1 (
    .e1(c1), .e0(c0), .s3(decodificador_1_s3), .s2(decodificador_1_s2), .s1(decodificador_1_s1),
    .s0(decodificador_1_s0));
  and and_1 (s3, decodificador_1_s3, e0);
  and and_2 (s2, decodificador_1_s2, e0);
  and and_3 (s1, decodificador_1_s1, e0);
  and and_4 (s0, decodificador_1_s0, e0);
endmodule

module Codificador (
  input  e0,
  input  e1,
  input  e2,
  input  e3,
  output v,
  output s1,
  output s0
);

  wire and_1_out, nor_1_out, nor_2_out, nor_3_out, xor_1_out, xor_2_out, xor_3_out;

  xor xor_1 (xor_1_out, e0, e1);
  nor nor_1 (nor_1_out, e2, e3);
  nor nor_2 (nor_2_out, e0, e1);
  xor xor_2 (xor_2_out, e2, e3);
  nor nor_3 (nor_3_out, e0, e2);
  xor xor_3 (xor_3_out, e1, e3);
  and and_1 (and_1_out, xor_1_out, nor_1_out);
  and and_2 (s1, nor_2_out, xor_2_out);
  and and_3 (s0, nor_3_out, xor_3_out);
  or or_1 (v, and_1_out, s1);
endmodule

module Decodificador (
  input  e1,
  input  e0,
  output s3,
  output s2,
  output s1,
  output s0
);

  wire not_1_out, not_2_out;

  not not_1 (not_1_out, e1);
  not not_2 (not_2_out, e0);
  and and_1 (s3, e1, e0);
  and and_2 (s2, e1, not_2_out);
  and and_3 (s1, not_1_out, e0);
  and and_4 (s0, not_1_out, not_2_out);
endmodule

module CarryLeftShifter (
  input  c,
  input  e2,
  input  e1,
  input  e0,
  output s3,
  output s2,
  output s1,
  output s0
);

  wire and_1_out, and_2_out, and_3_out, and_4_out, not_1_out, not_2_out, not_3_out, not_4_out;

  not not_1 (not_1_out, c);
  not not_2 (not_2_out, e2);
  not not_3 (not_3_out, e1);
  not not_4 (not_4_out, e0);
  and and_1 (and_1_out, not_1_out, e2);
  and and_2 (and_2_out, c, e1);
  and and_3 (and_3_out, not_1_out, e1);
  and and_4 (and_4_out, c, e0);
  and and_5 (s3, c, e2);
  or or_1 (s2, and_1_out, and_2_out);
  or or_2 (s1, and_3_out, and_4_out);
  and and_6 (s0, not_1_out, e0);
endmodule

module FullAdder1bit (
  input  A,
  input  B,
  input  Cin,
  output S,
  output Cout
);

  wire and_1_out, and_2_out, xor_1_out;

  xor xor_1 (xor_1_out, A, B);
  xor xor_2 (S, xor_1_out, Cin);
  and and_1 (and_1_out, xor_1_out, Cin);
  or or_1 (Cout, and_1_out, and_2_out);
  and and_2 (and_2_out, A, B);
endmodule

module FullAdder4bitsV1 (
  input  A3,
  input  A2,
  input  A1,
  input  A0,
  input  B3,
  input  B2,
  input  B1,
  input  B0,
  output C,
  output S3,
  output S2,
  output S1,
  output S0
);

  wire fulladder1bit_2_cout, fulladder1bit_3_cout, fulladder1bit_4_cout;

  FullAdder1bit fulladder1bit_1 (.A(A3), .B(B3), .Cin(fulladder1bit_2_cout), .S(S3), .Cout(C));
  FullAdder1bit fulladder1bit_2 (.A(A2), .B(B2), .Cin(fulladder1bit_3_cout), .S(S2), .Cout(fulladder1bit_2_cout));
  FullAdder1bit fulladder1bit_3 (.A(A1), .B(B1), .Cin(fulladder1bit_4_cout), .S(S1), .Cout(fulladder1bit_3_cout));
  FullAdder1bit fulladder1bit_4 (.A(A0), .B(B0), .S(S0), .Cout(fulladder1bit_4_cout));  // open: Cin

  // Notes on the sheet:
  //   +
endmodule

module FullAdder4bitsV2 (
  input  A3,
  input  A2,
  input  A1,
  input  A0,
  input  B3,
  input  B2,
  input  B1,
  input  B0,
  output S3,
  output S2,
  output S1,
  output S0,
  output Z,
  output N,
  output C,
  output V
);

  wire fulladder1bit_2_cout, fulladder1bit_3_cout, fulladder1bit_4_cout, nor_1_out, nor_2_out;

  FullAdder1bit fulladder1bit_1 (.A(A3), .B(B3), .Cin(fulladder1bit_2_cout), .S(N), .Cout(C));
  FullAdder1bit fulladder1bit_2 (.A(A2), .B(B2), .Cin(fulladder1bit_3_cout), .S(S2), .Cout(fulladder1bit_2_cout));
  FullAdder1bit fulladder1bit_3 (.A(A1), .B(B1), .Cin(fulladder1bit_4_cout), .S(S1), .Cout(fulladder1bit_3_cout));
  FullAdder1bit fulladder1bit_4 (.A(A0), .B(B0), .S(S0), .Cout(fulladder1bit_4_cout));  // open: Cin
  nor nor_1 (nor_1_out, N, S2);
  nor nor_2 (nor_2_out, S1, S0);
  and and_1 (Z, nor_1_out, nor_2_out);
  xor xor_1 (V, C, fulladder1bit_2_cout);

  assign S3 = N;

  // Notes on the sheet:
  //   +
endmodule

module Negator4bits (
  input  e3,
  input  e2,
  input  e1,
  input  e0,
  output s3,
  output s2,
  output s1,
  output s0
);

  not not_1 (s3, e3);
  not not_2 (s2, e2);
  not not_3 (s1, e1);
  not not_4 (s0, e0);
endmodule

module Inverter4bitsV1 (
  input  e3,
  input  e2,
  input  e1,
  input  e0,
  output s3,
  output s2,
  output s1,
  output s0
);

  wire negator4bits_1_s0, negator4bits_1_s1, negator4bits_1_s2, negator4bits_1_s3, undriven;

  Negator4bits negator4bits_1 (
    .e3(e3), .e2(e2), .e1(e1), .e0(e0), .s3(negator4bits_1_s3), .s2(negator4bits_1_s2),
    .s1(negator4bits_1_s1), .s0(negator4bits_1_s0));
  FullAdder4bitsV2 fulladder4bitsv2_1 (
    .A3(negator4bits_1_s3), .A2(negator4bits_1_s2), .A1(negator4bits_1_s1), .A0(negator4bits_1_s0),
    .B3(undriven), .B2(1'b0), .B1(undriven), .B0(1'b1), .S3(s3), .S2(s2), .S1(s1), .S0(s0));  // open: Z, N, C, V
endmodule

module Inverter4bitsV2 (
  input  e3,
  input  e2,
  input  e1,
  input  e0,
  output F,
  output s3,
  output s2,
  output s1,
  output s0
);

  wire and_1_out, and_2_out, negator4bits_1_s0, negator4bits_1_s1, negator4bits_1_s2, negator4bits_1_s3,
       undriven;

  Negator4bits negator4bits_1 (
    .e3(e3), .e2(e2), .e1(e1), .e0(e0), .s3(negator4bits_1_s3), .s2(negator4bits_1_s2),
    .s1(negator4bits_1_s1), .s0(negator4bits_1_s0));
  and and_1 (and_1_out, negator4bits_1_s0, negator4bits_1_s1);
  and and_2 (and_2_out, and_1_out, negator4bits_1_s2);
  FullAdder4bitsV2 fulladder4bitsv2_1 (
    .A3(negator4bits_1_s3), .A2(negator4bits_1_s2), .A1(negator4bits_1_s1), .A0(negator4bits_1_s0),
    .B3(undriven), .B2(1'b0), .B1(undriven), .B0(1'b1), .S3(s3), .S2(s2), .S1(s1), .S0(s0));  // open: Z, N, C, V
  and and_3 (F, e3, and_2_out);
endmodule
