// Logisim project Práctica2.circ as structural Verilog: 15 circuits, main circuit NAND_AND
module NAND_AND (
  input  p,
  input  q,
  output pANDq
);

  wire nand_1_out;

  nand nand_1 (nand_1_out, p, q);
  nand nand_2 (pANDq, nand_1_out, nand_1_out);
endmodule

module NAND_NOT (
  input  p,
  output NOTp
);

  nand nand_1 (NOTp, p, p);
endmodule

module NAND_OR (
  input  p,
  input  q,
  output pORq
);

  wire nand_1_out, nand_2_out;

  nand nand_1 (nand_1_out, p, p);
  nand nand_2 (nand_2_out, q, q);
  nand nand_3 (pORq, nand_1_out, nand_2_out);
endmodule

module NOR_NOT (
  input  p,
  output NOTp
);

  nor nor_1 (NOTp, p, p);
endmodule

module NOR_AND (
  input  p,
  input  q,
  output pANDq
);

  wire nor_1_out, nor_2_out;

  nor nor_1 (nor_1_out, p, p);
  nor nor_2 (nor_2_out, q, q);
  nor nor_3 (pANDq, nor_1_out, nor_2_out);
endmodule

module NOR_OR (
  input  p,
  input  q,
  output pORq
);

  wire nor_1_out;

  nor nor_1 (nor_1_out, p, q);
  nor nor_2 (pORq, nor_1_out, nor_1_out);
endmodule

module P2_EJ5 (
  input  p,
  input  q,
  input  r,
  output pANDqANDr
);

  wire nor_1_out, not_1_out, not_2_out, not_3_out, not_4_out;

  not not_1 (not_1_out, p);
  not not_2 (not_2_out, q);
  not not_3 (not_3_out, r);
  nor nor_1 (nor_1_out, not_1_out, not_2_out);
  not not_4 (not_4_out, nor_1_out);
  nor nor_2 (pANDqANDr, not_4_out, not_3_out);
endmodule

module P2_EJ6 (
  input  A,
  input  B,
  input  C,
  output RES
);

  wire and_1_out, and_2_out, not_1_out;

  not not_1 (not_1_out, B);
  and and_1 (and_1_out, A, not_1_out);
  and and_2 (and_2_out, B, C);
  or or_1 (RES, and_1_out, and_2_out);
endmodule

module Demultiplexor_v1 (
  input  e0,
  input  c1,
  input  c0,
  output s3,
  output s2,
  output s1,
  output s0
);

  wire and_1_out, and_3_out, and_5_out, and_7_out, not_1_out, not_2_out;

  not not_1 (not_1_out, c1);
  not not_2 (not_2_out, c0);
  and and_1 (and_1_out, c1, c0);
  and and_2 (s3, and_1_out, e0);
  and and_3 (and_3_out, c1, not_2_out);
  and and_4 (s2, and_3_out, e0);
  and and_5 (and_5_out, not_1_out, c0);
  and and_6 (s1, and_5_out, e0);
  and and_7 (and_7_out, not_1_out, not_2_out);
  and and_8 (s0, and_7_out, e0);
endmodule

module Demultiplexor_v2 (
  input  e0,
  input  c1,
  input  c0,
  output s3,
  output s2,
  output s1,
  output s0
);

  wire decodificador_1_s0, decodificador_1_s1, decodificador_1_s2, decodificador_1_s3;

  Decodificador decodificador_1 (
    .e1(c1), .e0(c0), .s3(decodificador_1_s3), .s2(decodificador_1_s2), .s1(decodificador_1_s1),
    .s0(decodificador_1_s0));
  and and_1 (s3, decodificador_1_s3, e0);
  and and_2 (s2, decodificador_1_s2, e0);
  and and_3 (s1, decodificador_1_s1, e0);
  and and_4 (s0, decodificador_1_s0, e0);
endmodule

module Codificador_v1 (
  input  e0,
  input  e1,
  input  e2,
  input  e3,
  output s1,
  output s0
);

  wire and_1_out, and_2_out, and_3_out, and_4_out, and_5_out, and_6_out, and_7_out, and_8_out, and_9_out,
       not_1_out, not_2_out, not_3_out, not_4_out;

  not not_1 (not_1_out, e0);
  not not_2 (not_2_out, e1);
  not not_3 (not_3_out, e2);
  not not_4 (not_4_out, e3);
  and and_1 (and_1_out, not_1_out, not_2_out);
  and and_2 (and_2_out, not_1_out, not_2_out);
  and and_3 (and_3_out, not_1_out, not_3_out);
  and and_4 (and_4_out, and_1_out, not_4_out);
  and and_5 (and_5_out, and_4_out, e2);
  and and_6 (and_6_out, and_2_out, not_3_out);
  and and_7 (and_7_out, and_6_out, e3);
  and and_8 (and_8_out, and_3_out, not_4_out);
  and and_9 (and_9_out, and_8_out, e1);
  or or_1 (s1, and_5_out, and_7_out);
  or or_2 (s0, and_7_out, and_9_out);
endmodule

module Codificador_v2 (
  input  e0,
  input  e1,
  input  e2,
  input  e3,
  output s1,
  output s0,
  output v
);

  wire and_1_out, and_2_out, and_3_out, and_4_out, and_5_out, and_6_out, and_7_out, and_8_out, and_9_out,
       and_10_out, and_11_out, nor_1_out, nor_2_out, not_1_out, not_2_out, not_3_out, not_4_out, xor_1_out,
       xor_2_out;

  not not_1 (not_1_out, e0);
  not not_2 (not_2_out, e1);
  not not_3 (not_3_out, e2);
  not not_4 (not_4_out, e3);
  and and_1 (and_1_out, not_1_out, not_2_out);
  and and_2 (and_2_out, not_1_out, not_2_out);
  and and_3 (and_3_out, not_1_out, not_3_out);
  xor xor_1 (xor_1_out, e0, e1);
  xor xor_2 (xor_2_out, e2, e3);
  and and_4 (and_4_out, and_1_out, not_4_out);
  and and_5 (and_5_out, and_4_out, e2);
  and and_6 (and_6_out, and_2_out, not_3_out);
  and and_7 (and_7_out, and_6_out, e3);
  and and_8 (and_8_out, and_3_out, not_4_out);
  and and_9 (and_9_out, and_8_out, e1);
  and and_10 (and_10_out, xor_1_out, nor_1_out);
  nor nor_1 (nor_1_out, e2, e3);
  nor nor_2 (nor_2_out, e0, e1);
  and and_11 (and_11_out, nor_2_out, xor_2_out);
  or or_1 (s1, and_5_out, and_7_out);
  or or_2 (s0, and_7_out, and_9_out);
  or or_3 (v, and_10_out, and_11_out);
endmodule

module Decodificador (
  input  e1,
  input  e0,
  output s3,
  output s2,
  output s1,
  output s0
);

  wire not_1_out, not_2_out;

  not not_1 (not_1_out, e1);
  not not_2 (not_2_out, e0);
  and and_1 (s3, e1, e0);
  and and_2 (s2, e1, not_2_out);
  and and_3 (s1, not_1_out, e0);
  and and_4 (s0, not_1_out, not_2_out);
endmodule

module CarryLeftShifter (
  input  c,
  input  e2,
  input  e1,
  input  e0,
  output s3,
  output s2,
  output s1,
  output s0
);

  wire and_1_out, and_2_out, and_3_out, and_4_out, not_1_out, not_2_out, not_3_out, not_4_out;

  not not_1 (not_1_out, c);
  not not_2 (not_2_out, e2);
  not not_3 (not_3_out, e1);
  not not_4 (not_4_out, e0);
  and and_1 (and_1_out, not_1_out, e2);
  and and_2 (and_2_out, c, e1);
  and and_3 (and_3_out, not_1_out, e1);
  and and_4 (and_4_out, c, e0);
  and and_5 (s3, c, e2);
  or or_1 (s2, and_1_out, and_2_out);
  or or_2 (s1, and_3_out, and_4_out);
  and and_6 (s0, not_1_out, e0);
endmodule

module FullAdder (
  input  A,
  input  B,
  input  Cin,
  output suma,
  output Cout
);

  wire and_1_out, and_2_out, xor_1_out;

  xor xor_1 (xor_1_out, A, B);
  xor xor_2 (suma, xor_1_out, Cin);
  and and_1 (and_1_out, xor_1_out, Cin);
  or or_1 (Cout, and_1_out, and_2_out);
  and and_2 (and_2_out, A, B);
endmodule
