// Logisim project p1.circ as structural Verilog: 9 circuits, main circuit NAND_AND
module NAND_AND (
  input  p,
  input  q,
  output pANDq
);

  wire nand_1_out;

  nand nand_1 (nand_1_out, p, q);
  nand nand_2 (pANDq, nand_1_out, nand_1_out);
endmodule

module NAND_NOT (
  input  p,
  output NOTp
);

  nand nand_1 (NOTp, p, p);
endmodule

module NAND_OR (
  input  p,
  input  q,
  output pORq
);

  wire nand_1_out, nand_2_out;

  nand nand_1 (nand_1_out, p, p);
  nand nand_2 (nand_2_out, q, q);
  nand nand_3 (pORq, nand_1_out, nand_2_out);
endmodule

module NOR_NOT (
  input  p,
  output NOTp
);

  nor nor_1 (NOTp, p, p);
endmodule

module NOR_AND (
  input  p,
  input  q,
  output pANDq
);

  wire nor_1_out, nor_2_out;

  nor nor_1 (nor_1_out, p, p);
  nor nor_2 (nor_2_out, q, q);
  nor nor_3 (pANDq, nor_1_out, nor_2_out);
endmodule

module NOR_OR (
  input  p,
  input  q,
  output pORq
);

  wire nor_1_out;

  nor nor_1 (nor_1_out, p, q);
  nor nor_2 (pORq, nor_1_out, nor_1_out);
endmodule

module p1_ej5 (
  input  p,
  input  q,
  input  r,
  output pANDqANDr
);

  wire nor_1_out, not_1_out, not_2_out, not_3_out, not_4_out;

  not not_1 (not_1_out, p);
  not not_2 (not_2_out, q);
  not not_3 (not_3_out, r);
  nor nor_1 (nor_1_out, not_1_out, not_2_out);
  not not_4 (not_4_out, nor_1_out);
  nor nor_2 (pANDqANDr, not_4_out, not_3_out);
endmodule

module p1_ej6 (
  input  A,
  input  B,
  input  C,
  output RES
);

  wire and_1_out, and_2_out, not_1_out;

  not not_1 (not_1_out, B);
  and and_1 (and_1_out, A, not_1_out);
  and and_2 (and_2_out, B, C);
  or or_1 (RES, and_1_out, and_2_out);
endmodule

module p1_ej7 (
  input  e0,
  input  c1,
  input  c0,
  output s0,
  output s1,
  output s2,
  output s3
);

  wire and_1_out, and_2_out, and_3_out, and_4_out, not_1_out, not_2_out;

  not not_1 (not_1_out, c1);
  not not_2 (not_2_out, c0);
  and and_1 (and_1_out, not_1_out, not_2_out);
  and and_2 (and_2_out, not_1_out, c0);
  and and_3 (and_3_out, c1, not_2_out);
  and and_4 (and_4_out, c1, c0);
  and and_5 (s0, and_1_out, e0);
  and and_6 (s1, and_2_out, e0);
  and and_7 (s2, and_3_out, e0);
  and and_8 (s3, and_4_out, e0);
endmodule
