// Logisim project p1_ej3.circ as structural Verilog: 6 circuits, main circuit NAND_AND
module NAND_AND (
  input  p,
  input  q,
  output pANDq
);

  wire nand_1_out;

  nand nand_1 (nand_1_out, p, q);
  nand nand_2 (pANDq, nand_1_out, nand_1_out);
endmodule

module NAND_NOT (
  input  p,
  output NOTp
);

  nand nand_1 (NOTp, p, p);
endmodule

module NAND_OR (
  input  p,
  input  q,
  output pORq
);

  wire nand_1_out, nand_2_out;

  nand nand_1 (nand_1_out, p, p);
  nand nand_2 (nand_2_out, q, q);
  nand nand_3 (pORq, nand_1_out, nand_2_out);
endmodule

module NOR_NOT (
  input  p,
  output NOTp
);

  nor nor_1 (NOTp, p, p);
endmodule

module NOR_AND (
  input  p,
  input  q,
  output pANDq
);

  wire nor_1_out, nor_2_out;

  nor nor_1 (nor_1_out, p, p);
  nor nor_2 (nor_2_out, q, q);
  nor nor_3 (pANDq, nor_1_out, nor_2_out);
endmodule

module NOR_OR (
  input  p,
  input  q,
  output pORq
);

  wire nor_1_out;

  nor nor_1 (nor_1_out, p, q);
  nor nor_2 (pORq, nor_1_out, nor_1_out);
endmodule
