// Logisim project TallerLogica-Combinatorios.circ as structural Verilog: 15 circuits, main circuit verificador
module sumador_simple (
  input  a,
  input  b,
  output S,
  output Cout
);

  xor xor_1 (S, a, b);
  and and_1 (Cout, a, b);
endmodule

module sumador_completo (
  input  Cin,
  input  A,
  input  B,
  output S,
  output Cout
);

  wire and_1_out, and_2_out, xor_1_out;

  and and_1 (and_1_out, A, B);
  or or_1 (Cout, and_1_out, and_2_out);
  xor xor_1 (xor_1_out, A, B);
  and and_2 (and_2_out, xor_1_out, Cin);
  xor xor_2 (S, Cin, xor_1_out);
endmodule

module sumador_4 (
  input  [3:0] A,
  input  [3:0] B,
  input  Cin,
  output [3:0] S,
  output Cout
);

  wire sumador_completo_1_cout, sumador_completo_2_cout, sumador_completo_3_cout;

  sumador_completo sumador_completo_1 (.A(A[0]), .B(B[0]), .Cin(Cin), .Cout(sumador_completo_1_cout), .S(S[0]));
  sumador_completo sumador_completo_2 (
    .A(A[1]), .B(B[1]), .Cin(sumador_completo_1_cout), .Cout(sumador_completo_2_cout), .S(S[1]));
  sumador_completo sumador_completo_3 (
    .A(A[2]), .B(B[2]), .Cin(sumador_completo_2_cout), .Cout(sumador_completo_3_cout), .S(S[2]));
  sumador_completo sumador_completo_4 (.A(A[3]), .B(B[3]), .Cin(sumador_completo_3_cout), .Cout(Cout), .S(S[3]));
  Hex_Digit_Display hex_digit_display_1 (.value(S));  // open: dp
endmodule

module comparador_cero (
  input  [3:0] A,
  output Z
);

  wire or_1_out, or_2_out, or_3_out;

  or or_1 (or_1_out, A[0], A[1]);
  or or_2 (or_2_out, A[2], A[3]);
  or or_3 (or_3_out, or_1_out, or_2_out);
  not not_1 (Z, or_3_out);
endmodule

module sumador_flags (
  input  Cin,
  input  [3:0] A,
  input  [3:0] B,
  output [3:0] S,
  output N,
  output Z,
  output V,
  output C
);

  Hex_Digit_Display hex_digit_display_1 (.value(A));  // open: dp
  Hex_Digit_Display hex_digit_display_2 (.value(B));  // open: dp
  sumador_4 sumador_4_1 (.Cin(Cin), .A(A), .S(S), .Cout(C), .B(B));
  Hex_Digit_Display hex_digit_display_3 (.value(S));  // open: dp
  negativo_comp2 negativo (.S(S), .N(N));
  comparador_cero comparador_cero (.A(S), .Z(Z));
  overflow_comp2 overflow (.A(A), .B(B), .S(S), .V(V));  // open: OP
endmodule

module incrementador_4 (
  input  [3:0] A,
  output [3:0] S
);

  sumador_4 sumador_4_1 (.Cin(1'b1), .A(A), .S(S), .B(4'b0000));  // open: Cout
  Hex_Digit_Display hex_digit_display_1 (.value(S));  // open: dp
endmodule

module inversor_aditivo_4 (
  input  [3:0] A,
  input  INV,
  output [3:0] S
);

  wire [3:0] xor_1_out;

  xor xor_1 (xor_1_out[0], A[0], INV);
  xor xor_2 (xor_1_out[1], A[1], INV);
  xor xor_3 (xor_1_out[2], A[2], INV);
  xor xor_4 (xor_1_out[3], A[3], INV);
  sumador_4 sumador_4_1 (.Cin(INV), .A(xor_1_out), .S(S), .B(4'b0000));  // open: Cout
  Hex_Digit_Display hex_digit_display_1 (.value(S));  // open: dp
endmodule

module ALU (
  input  [3:0] A,
  input  [3:0] B,
  input  [1:0] OP,
  output N,
  output Z,
  output V,
  output C,
  output [3:0] S
);

  wire borrow_borrow, multiplexer_1_out, not_1_out, overflow_v, sumador_4_1_cout;
  wire [3:0] and_or_s, inversor_s, sumador_4_1_s;

  inversor_aditivo_4 inversor (.A(B), .INV(OP[0]), .S(inversor_s));
  borrow borrow (.A(A), .B(B), .S(sumador_4_1_s), .BORROW(borrow_borrow));
  overflow_comp2 overflow (.A(A), .B(B), .S(sumador_4_1_s), .OP(OP[0]), .V(overflow_v));
  sumador_4 sumador_4_1 (.Cin(1'b0), .A(A), .S(sumador_4_1_s), .Cout(sumador_4_1_cout), .B(inversor_s));
  and_or_4 and_or (.A(A), .B(B), .OP(OP[0]), .S(and_or_s));
  Multiplexer #(.disabled(0), .enable("false")) multiplexer_1 (
    .in0(sumador_4_1_cout), .in1(borrow_borrow), .out(multiplexer_1_out), .sel(OP[0]));
  Multiplexer #(.width(4), .disabled(0), .enable("false")) multiplexer_2 (
    .in0(sumador_4_1_s), .in1(and_or_s), .out(S), .sel(OP[1]));
  not not_1 (not_1_out, OP[1]);
  negativo_comp2 negativo (.S(S), .N(N));
  comparador_cero comparador_cero (.A(S), .Z(Z));
  and and_1 (V, overflow_v, not_1_out);
  and and_2 (C, multiplexer_1_out, not_1_out);
  Hex_Digit_Display hex_digit_display_1 (.value(S));  // open: dp
endmodule

module verificador (
  output [3:0] a,
  output [3:0] b,
  output [1:0] Op,
  output N,
  output Z,
  output V,
  output C,
  output [3:0] Res,
  output halt
);

  wire clock_1_out;

  Clock clock_1 (.out(clock_1_out));
  Counter #(.width(10), .max('h3ff)) counter_1 (
    .Q({Op, b, a}), .carry(halt), .clk(clock_1_out));  // open: load, D, count, clr
  ALU alu_1 (.A(a), .B(b), .OP(Op), .N(N), .Z(Z), .V(V), .C(C), .S(Res));
endmodule

module overflow_comp2 (
  input  [3:0] A,
  input  [3:0] B,
  input  [3:0] S,
  input  OP,
  output V
);

  wire and_1_out, and_2_out, not_1_out, not_2_out, xor_1_out, xor_2_out, xor_3_out, xor_4_out;

  xor xor_1 (xor_1_out, A[3], B[3]);
  xor xor_2 (xor_2_out, A[3], S[3]);
  xor xor_3 (xor_3_out, S[3], B[3]);
  xor xor_4 (xor_4_out, S[3], A[3]);
  not not_1 (not_1_out, xor_1_out);
  not not_2 (not_2_out, xor_3_out);
  and and_1 (and_1_out, not_1_out, xor_2_out);
  and and_2 (and_2_out, not_2_out, xor_4_out);
  Multiplexer #(.enable("false")) multiplexer_1 (.in0(and_1_out), .in1(and_2_out), .out(V), .sel(OP));
endmodule

module negativo_comp2 (
  input  [3:0] S,
  output N
);


  assign N = S[3];
endmodule

module and_or_4 (
  input  [3:0] A,
  input  [3:0] B,
  input  OP,
  output [3:0] S
);

  wire [3:0] and_4_1_s, inversor_4_1_s, inversor_4_2_s;

  inversor_4 inversor_4_1 (.A(A), .INV(OP), .S(inversor_4_1_s));
  inversor_4 inversor_4_2 (.A(B), .INV(OP), .S(inversor_4_2_s));
  and_4 and_4_1 (.A(inversor_4_1_s), .B(inversor_4_2_s), .S(and_4_1_s));
  inversor_4 inversor_4_3 (.A(and_4_1_s), .INV(OP), .S(S));
endmodule

module inversor_4 (
  input  [3:0] A,
  input  INV,
  output [3:0] S
);

  xor xor_1 (S[0], A[0], INV);
  xor xor_2 (S[1], A[1], INV);
  xor xor_3 (S[2], A[2], INV);
  xor xor_4 (S[3], A[3], INV);
endmodule

module and_4 (
  input  [3:0] A,
  input  [3:0] B,
  output [3:0] S
);

  and and_1 (S[0], A[0], B[0]);
  and and_2 (S[1], A[1], B[1]);
  and and_3 (S[2], A[2], B[2]);
  and and_4 (S[3], A[3], B[3]);
endmodule

module borrow (
  input  [3:0] A,
  input  [3:0] B,
  input  [3:0] S,
  output BORROW
);

  wire and_1_out, and_2_out, not_1_out, not_2_out, xor_1_out;

  not not_1 (not_1_out, A[3]);
  and and_1 (and_1_out, not_1_out, B[3]);
  xor xor_1 (xor_1_out, A[3], B[3]);
  not not_2 (not_2_out, xor_1_out);
  and and_2 (and_2_out, not_2_out, S[3]);
  or or_1 (BORROW, and_1_out, and_2_out);
endmodule
