// Logisim project ALU-para-prestar.circ as structural Verilog: 1 circuit, main circuit ALU
module ALU (
  input  [3:0] A,
  input  [3:0] B,
  input  [1:0] OP,
  output N,
  output Z,
  output V,
  output C,
  output [3:0] S
);

  wire adder_1_cout, and_2_out, or_2_out, subtractor_1_bout, xnor_1_out, xor_1_out, xor_2_out;
  wire [3:0] adder_1_out, and_1_out, or_1_out, subtractor_1_out;

  xor xor_1 (xor_1_out, B[3], OP[0]);
  Subtractor #(.width(4)) subtractor_1 (.a(A), .b(B), .out(subtractor_1_out), .bout(subtractor_1_bout));  // open: bin
  xnor xnor_1 (xnor_1_out, A[3], xor_1_out);
  Adder #(.width(4)) adder_1 (.a(A), .b(B), .out(adder_1_out), .cout(adder_1_cout));  // open: cin
  assign and_1_out = A & B;  // AND_Gate and_1, 4 bits wide
  assign or_1_out = A | B;  // OR_Gate or_1, 4 bits wide
  xor xor_2 (xor_2_out, xor_1_out, N);
  and and_2 (and_2_out, xnor_1_out, xor_2_out);
  Multiplexer #(.select(2), .width(4)) multiplexer_1 (
    .in0(adder_1_out), .in1(subtractor_1_out), .in2(and_1_out), .in3(or_1_out), .out({N, S[2:0]}), .sel(OP));  // open: en
  Multiplexer #(.select(2)) multiplexer_2 (
    .in0(and_2_out), .in1(and_2_out), .in2(1'b0), .in3(1'b0), .out(V), .sel(OP));  // open: en
  Multiplexer #(.select(2)) multiplexer_3 (
    .in0(adder_1_cout), .in1(subtractor_1_bout), .in2(1'b0), .in3(1'b0), .out(C), .sel(OP));  // open: en
  or or_2 (or_2_out, S[0], S[1], S[2], N);
  not not_1 (Z, or_2_out);
  Hex_Digit_Display hex_digit_display_1 (.value({N, S[2:0]}));  // open: dp

  assign S[3] = N;
endmodule
